# Fritzing sketch wiring fritzing (saved by Fritzing 1.0.7)

parts:
  Part1 = InvenSense MPU6050
  M1 = DOIT Esp32 DevKit v1 (30 pins long, 11 pins width) [part_number=ESP32S-PIN30]
  VCC1 = Battery
  M2 = 3S 40A Li-ion Lithium Battery Charger Cell Module PCB BMS Protection Board
  Part3 = FC-28 Soil Hygrometer Module - Probe
  Part4 = FC-28 Soil Hygrometer Module
  S1 = Square Pushbutton
  J1 = Power Jack [package=power_jack_pth]

nets:
  VCC: Part1.VCC, M1.VN, Part4.VCC
  GND: Part1.GND, M1.GND, M2.pin_6, Part4.GND, J1.GND
  N1: Part1.SCL, M1.D22
  N2: Part1.SDA, M1.D21
  N3: M1.D12, Part4.AO
  N4: M1.VIN, S1.leg0
  N5: VCC1.-, M2.Pin_1
  N6: VCC1.+, M2.Pin_4
  N7: M2.pin_5, S1.leg1, J1.PWR
  N8: Part3.POS, Part4.POS
  N9: Part3.NEG, Part4.NEG

custom parts:
  DOIT Esp32 DevKit v1 (30 pins long, 11 pins width): The DOIT Esp32 DevKit v1 is one of the development board created by DOIT to evaluate the ESP-WROOM-32 module. It is based on the ESP32 microcontroller that boasts Wifi, Bluetooth, Ethernet and Low Power support all in a single chip. (vanepp) made breadboard work, adjusted pin numbering and labels and reduced size of schematic and cleaned up pcb. This chip is 30pins long (2 x15) and 11 pins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
  Battery: Your standard 3x 18650 battery pack (11.1 Volts)
  FC-28 Soil Hygrometer Module - Probe: The FC-28 is a soil hygrometer module that uses the Texas Instruments LM393 comparator chip to provide an analog measurement of soil humidity.
  FC-28 Soil Hygrometer Module: The FC-28 is a soil hygrometer module that uses the Texas Instruments LM393 comparator chip to provide an analog measurement of soil humidity. The digital output is high when soil moisture is over a certain threshold, as determined by adjusting the potentiometer.
